# Fritzing sketch Schematic (saved by Fritzing 0.9.3b)
breadboards: 1

parts:
  U1 = ESP8266-12e_tht [part_number=ESP8266-12E]
  U2 = attiny85 [part_number=. package=dip]
  PGM_protect_JMP = Header 2 [package=springterminal-2.54mm-2]
  part = Resistor [tolerance=±5% resistance=10k package=THT]
  RST/MO/MI/SC_programming = female pin header, 4 pins [form="♀ (female)"]
  part_2 = Resistor [tolerance=±5% resistance=10k package=THT]
  part_3 = Resistor [tolerance=±5% resistance=10k package=THT]
  TX/RX/PGM_programming = female pin header, 3 pins [form="♀ (female)"]
  TSL2541 = IC, SIP package, 4 pins
  SI7021 = IC, SIP package, 4 pins

nets:
  N1: U1.REST, PGM_protect_JMP.2
  N2: U1.CH_PD, part.Pin_0
  3.3V: U1.VCC, U2.Pin_8, part.Pin_1, part_3.Pin_1
  GND: U1.GND, U2.Pin_4, part_2.Pin_1, TSL2541.pin3, SI7021.pin2
  N3: U1.GPIO_15, part_2.Pin_0
  N4: U1.GPIO_0, part_3.Pin_0, TX/RX/PGM_programming.pin3
  N5: U1.GPIO_4, U2.Pin_5, RST/MO/MI/SC_programming.pin3, TSL2541.pin1, SI7021.pin4
  N6: U1.GPIO_5, U2.Pin_7, RST/MO/MI/SC_programming.pin1, TSL2541.pin2, SI7021.pin3
  N7: U1.GPIO_3/RXD, TX/RX/PGM_programming.pin2
  N8: U1.GPIO_1/TXD, TX/RX/PGM_programming.pin1
  N9: U2.Pin_1, RST/MO/MI/SC_programming.pin4
  N10: U2.Pin_3, TSL2541.pin4, SI7021.pin1
  N11: U2.Pin_6, PGM_protect_JMP.1, RST/MO/MI/SC_programming.pin2

custom parts:
  ESP8266-12e_tht: These are the first series of modules made with the ESP8266 by the third-party manufacturer AI-Thinker and remain the most widely available. They are collectively referred to as "ESP-xx modules" and to form a workable development system require additional components, especially a serial TTL-to-USB adapter (sometimes called a USB-to-UART bridge) and an external 3.3V power supply. The pcb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
